// Logisim project p8x-memory-card.circ as structural Verilog: 1 circuit, main circuit memory-card
module memory_card (
);


  // Notes on the sheet:
  //   J1 MABC96R (DIN96C)
  //   A1
  //   A2
  //   A3
  //   A4
  //   A5
  //   A6
  //   A7
  //   A8
  //   A9
  //   A10
  //   A11
  //   A12
  //   A13
  //   A14
  //   A15
  //   A16
  //   A17
  //   A18
  //   A19
  //   A20
  //   A21
  //   A22
  //   A23
  //   A24
  //   A25
  //   A26
  //   A27
  //   A28
  //   A29
  //   A30
  //   A31
  //   A32
  //   B1
  //   B2
  //   B3
  //   B4
  //   B5
  //   B6
  //   B7
  //   B8
  //   B9
  //   B10
  //   B11
  //   B12
  //   B13
  //   B14
  //   B15
  //   B16
  //   B17
  //   B18
  //   B19
  //   B20
  //   B21
  //   B22
  //   B23
  //   B24
  //   B25
  //   B26
  //   B27
  //   B28
  //   B29
  //   B30
  //   B31
  //   B32
  //   C1
  //   C2
  //   C3
  //   C4
  //   C5
  //   C6
  //   C7
  //   C8
  //   C9
  //   C10
  //   C11
  //   C12
  //   C13
  //   C14
  //   C15
  //   C16
  //   C17
  //   C18
  //   C19
  //   C20
  //   C21
  //   C22
  //   C23
  //   C24
  //   C25
  //   C26
  //   C27
  //   C28
  //   C29
  //   C30
  //   C31
  //   C32
  //   U1 28C256 (MEM28K8)
  //   A0
  //   A1
  //   A2
  //   A3
  //   A4
  //   A5
  //   A6
  //   A7
  //   A8
  //   A9
  //   A10
  //   A11
  //   A12
  //   A13
  //   A14
  //   IO0
  //   IO1
  //   IO2
  //   IO3
  //   IO4
  //   IO5
  //   IO6
  //   IO7
  //   !CE
  //   !OE
  //   !WE
  //   VCC
  //   GND
  //   U2 62256 (MEM28K8)
  //   A0
  //   A1
  //   A2
  //   A3
  //   A4
  //   A5
  //   A6
  //   A7
  //   A8
  //   A9
  //   A10
  //   A11
  //   A12
  //   A13
  //   A14
  //   IO0
  //   IO1
  //   IO2
  //   IO3
  //   IO4
  //   IO5
  //   IO6
  //   IO7
  //   !CE
  //   !OE
  //   !WE
  //   VCC
  //   GND
  //   U3 74HCT245 (74245)
  //   DIR
  //   A0
  //   A1
  //   A2
  //   A3
  //   A4
  //   A5
  //   A6
  //   A7
  //   !OE
  //   B0
  //   B1
  //   B2
  //   B3
  //   B4
  //   B5
  //   B6
  //   B7
  //   VCC
  //   GND
  //   U4 74HCT30 (7430)
  //   A
  //   B
  //   C
  //   D
  //   E
  //   F
  //   G
  //   H
  //   Y
  //   VCC
  //   GND
  //   U5 74HCT138 (74138)
  //   A
  //   B
  //   C
  //   G1
  //   !G2A
  //   !G2B
  //   Y0
  //   Y1
  //   Y2
  //   Y3
  //   Y4
  //   Y5
  //   Y6
  //   Y7
  //   VCC
  //   GND
  //   U6 74HCT138 (74138)
  //   A
  //   B
  //   C
  //   G1
  //   !G2A
  //   !G2B
  //   Y0
  //   Y1
  //   Y2
  //   Y3
  //   Y4
  //   Y5
  //   Y6
  //   Y7
  //   VCC
  //   GND
  //   U7 74HCT00 (GATES14)
  //   1A
  //   1B
  //   2A
  //   2B
  //   3A
  //   3B
  //   4A
  //   4B
  //   1Y
  //   2Y
  //   3Y
  //   4Y
  //   VCC
  //   GND
  //   U8 74HCT32 (GATES14)
  //   1A
  //   1B
  //   2A
  //   2B
  //   3A
  //   3B
  //   4A
  //   4B
  //   1Y
  //   2Y
  //   3Y
  //   4Y
  //   VCC
  //   GND
  //   U9 74HCT08 (GATES14)
  //   1A
  //   1B
  //   2A
  //   2B
  //   3A
  //   3B
  //   4A
  //   4B
  //   1Y
  //   2Y
  //   3Y
  //   4Y
  //   VCC
  //   GND
  //   U10 62256 (MEM28K8)
  //   A0
  //   A1
  //   A2
  //   A3
  //   A4
  //   A5
  //   A6
  //   A7
  //   A8
  //   A9
  //   A10
  //   A11
  //   A12
  //   A13
  //   A14
  //   IO0
  //   IO1
  //   IO2
  //   IO3
  //   IO4
  //   IO5
  //   IO6
  //   IO7
  //   !CE
  //   !OE
  //   !WE
  //   VCC
  //   GND
  //   RP1 1K (RES)
  //   1
  //   2
  //   LED3 GRN (LED)
  //   A
  //   K
  //   RS1 1K (RES)
  //   1
  //   2
  //   LED2 YEL (LED)
  //   A
  //   K
  //   RS2 1K (RES)
  //   1
  //   2
  //   LED4 YEL (LED)
  //   A
  //   K
  //   RS3 1K (RES)
  //   1
  //   2
  //   LED5 GRN (LED)
  //   A
  //   K
  //   RS4 1K (RES)
  //   1
  //   2
  //   LED6 RED (LED)
  //   A
  //   K
  //   RS5 1K (RES)
  //   1
  //   2
  //   LED7 YEL (LED)
  //   A
  //   K
  //   JWP 1x3 (HDR3)
  //   1
  //   2
  //   3
  //   CD1 100N (CAP1)
  //   1
  //   2
  //   CD2 100N (CAP1)
  //   1
  //   2
  //   CD3 100N (CAP1)
  //   1
  //   2
  //   CD4 100N (CAP1)
  //   1
  //   2
  //   CD5 100N (CAP1)
  //   1
  //   2
  //   CD6 100N (CAP1)
  //   1
  //   2
  //   CD7 100N (CAP1)
  //   1
  //   2
  //   CD8 100N (CAP1)
  //   1
  //   2
  //   CD9 100N (CAP1)
  //   1
  //   2
  //   CD10 100N (CAP1)
  //   1
  //   2
endmodule
